# Fritzing sketch zumo_rover (saved by Fritzing 0.9.3b)
breadboards: 1

parts:
  Onderdeel1 = Arduino Nano (Rev3.0)
  IC1 = L293D [package=THT]
  M1 = DC Motor
  M2 = DC Motor
  VCC1 = 4 x AAA Battery Mount
  Onderdeel2 = Bluetooth HC-05 Macho
  R1 = Resistor [tolerance=±5% resistance=1k package="2010 [SMD]"]
  R2 = Resistor [tolerance=±5% resistance=2.2k package="2010 [SMD]"]
  VCC2 = Battery block 9V

nets:
  GND: Onderdeel1.GND, IC1.0V, VCC1.-, Onderdeel2.GND, R2.Pin_1, VCC2.-
  N1: Onderdeel1.D2, IC1.In_2
  N2: Onderdeel1.D3, IC1.Enable_1
  N3: Onderdeel1.D4, IC1.In_1
  N4: Onderdeel1.D5, IC1.Enable_2
  N5: Onderdeel1.D6, IC1.In_3
  N6: Onderdeel1.D7, IC1.In_4
  N7: Onderdeel1.D9, R1.Pin_0
  N8: Onderdeel1.D11/MOSI, Onderdeel2.TXD
  N9: Onderdeel1.VIN, VCC2.+
  5V: Onderdeel1.5V, IC1.+V, Onderdeel2.VCC
  N10: IC1.Out_1_(_Controlled_by_Enable_1_), M2.pin_2
  N11: IC1.Out_2_(_Controlled_by_Enable_1_), M2.pin_1
  N12: IC1.+Vmotor, VCC1.+
  N13: IC1.Out_3_(_Controlled_by_Enable_2_), M1.pin_2
  N14: IC1.Out_4_(_Controlled_by_Enable_2_), M1.pin_1
  N15: Onderdeel2.RXD, R2.Pin_0
